// Logisim project onr-training.circ as structural Verilog
module main (
);

  wire button_1_out, clock_1_out, j_k_ff_1_qn, j_k_ff_2_qn, j_k_ff_3_qn, j_k_ff_4_qn, j_k_ff_5_qn,
       j_k_ff_6_qn, j_k_ff_7_qn, not_1_out, or_1_out, or_2_out, or_3_out, or_4_out, or_5_out, undriven;
  wire [3:0] j_k_ff_1_q, j_k_ff_5_q;

  Clock clock_1 (.out(clock_1_out));
  or or_1 (or_1_out, button_1_out, j_k_ff_5_q[3]);
  Button button_1 (.out(button_1_out));
  not not_1 (not_1_out, or_1_out);
  J_K_Flip_Flop j_k_ff_1 (
    .J(or_1_out), .clk(clock_1_out), .K(not_1_out), .Q(j_k_ff_1_q[0]), .Qn(j_k_ff_1_qn), .reset(undriven));  // open: preset, en
  J_K_Flip_Flop j_k_ff_2 (
    .J(j_k_ff_1_q[0]), .clk(clock_1_out), .K(j_k_ff_1_qn), .Q(j_k_ff_1_q[1]), .Qn(j_k_ff_2_qn),
    .reset(undriven));  // open: preset, en
  J_K_Flip_Flop j_k_ff_3 (
    .J(j_k_ff_1_q[1]), .clk(clock_1_out), .K(j_k_ff_2_qn), .Q(j_k_ff_1_q[2]), .Qn(j_k_ff_3_qn),
    .reset(undriven));  // open: preset, en
  J_K_Flip_Flop j_k_ff_4 (
    .J(j_k_ff_1_q[2]), .clk(clock_1_out), .K(j_k_ff_3_qn), .Q(j_k_ff_1_q[3]), .Qn(j_k_ff_4_qn),
    .reset(undriven));  // open: preset, en
  J_K_Flip_Flop j_k_ff_5 (
    .J(j_k_ff_1_q[3]), .clk(clock_1_out), .K(j_k_ff_4_qn), .Q(j_k_ff_5_q[0]), .Qn(j_k_ff_5_qn),
    .reset(undriven));  // open: preset, en
  or or_2 (or_2_out, j_k_ff_1_q[0], j_k_ff_5_q[3]);
  J_K_Flip_Flop j_k_ff_6 (
    .J(j_k_ff_5_q[1]), .clk(clock_1_out), .K(j_k_ff_7_qn), .Q(j_k_ff_5_q[2]), .Qn(j_k_ff_6_qn),
    .reset(undriven));  // open: preset, en
  J_K_Flip_Flop j_k_ff_7 (
    .J(j_k_ff_5_q[0]), .clk(clock_1_out), .K(j_k_ff_5_qn), .Q(j_k_ff_5_q[1]), .Qn(j_k_ff_7_qn),
    .reset(undriven));  // open: preset, en
  or or_3 (or_3_out, j_k_ff_1_q[1], j_k_ff_5_q[2]);
  or or_4 (or_4_out, j_k_ff_1_q[2], j_k_ff_5_q[1]);
  LED led_1 (.in(or_4_out));
  LED led_2 (.in(or_3_out));
  LED led_3 (.in(or_5_out));
  LED led_4 (.in(or_2_out));
  J_K_Flip_Flop j_k_ff_8 (
    .J(j_k_ff_5_q[2]), .clk(clock_1_out), .K(j_k_ff_6_qn), .Q(j_k_ff_5_q[3]), .reset(undriven));  // open: Qn, preset, en
  or or_5 (or_5_out, j_k_ff_1_q[3], j_k_ff_5_q[0]);

  // Notes on the sheet:
  //   CLK
  //   IN
endmodule
